// Logisim project hack-computer.circ as structural Verilog
module FullAdder (
  input  a,
  input  b,
  input  Cin,
  output Cout,
  output Sum
);

  wire and_1_out, and_2_out, and_3_out, xor_1_out;

  xor xor_1 (xor_1_out, a, b);
  and and_1 (and_1_out, a, b);
  and and_2 (and_2_out, b, Cin);
  and and_3 (and_3_out, Cin, a);
  xor xor_2 (Sum, xor_1_out, Cin);
  or or_1 (Cout, and_1_out, and_2_out, and_3_out);
endmodule

// adder
module _16bitAdder (
  input  x1,
  input  in_2,
  input  in_3,
  input  in_4,
  input  in_5,
  input  in_6,
  input  in_7,
  input  in_8,
  input  x9,
  input  in_10,
  input  in_11,
  input  in_12,
  input  in_13,
  input  in_14,
  input  in_15,
  input  x16,
  input  y1,
  input  in_18,
  input  in_19,
  input  in_20,
  input  in_21,
  input  in_22,
  input  in_23,
  input  in_24,
  input  y9,
  input  in_26,
  input  in_27,
  input  in_28,
  input  in_29,
  input  in_30,
  input  in_31,
  input  y16,
  input  c1,
  output overflow,
  output o1,
  output o2,
  output o3,
  output o4,
  output o5,
  output o6,
  output o7,
  output o8,
  output o9,
  output o10,
  output o11,
  output o12,
  output o13,
  output o14,
  output o15,
  output o16
);

  wire fulladder_2_cout, fulladder_3_cout, fulladder_4_cout, fulladder_5_cout, fulladder_6_cout,
       fulladder_7_cout, fulladder_8_cout, fulladder_9_cout, fulladder_10_cout, fulladder_11_cout,
       fulladder_12_cout, fulladder_13_cout, fulladder_14_cout, fulladder_15_cout, fulladder_16_cout;

  FullAdder fulladder_1 (.a(x1), .b(y1), .Cin(fulladder_2_cout), .Cout(overflow), .Sum(o1));
  FullAdder fulladder_2 (.a(in_2), .b(in_18), .Cin(fulladder_3_cout), .Cout(fulladder_2_cout), .Sum(o2));
  FullAdder fulladder_3 (.a(in_3), .b(in_19), .Cin(fulladder_4_cout), .Cout(fulladder_3_cout), .Sum(o3));
  FullAdder fulladder_4 (.a(in_4), .b(in_20), .Cin(fulladder_5_cout), .Cout(fulladder_4_cout), .Sum(o4));
  FullAdder fulladder_5 (.a(in_5), .b(in_21), .Cin(fulladder_6_cout), .Cout(fulladder_5_cout), .Sum(o5));
  FullAdder fulladder_6 (.a(in_6), .b(in_22), .Cin(fulladder_7_cout), .Cout(fulladder_6_cout), .Sum(o6));
  FullAdder fulladder_7 (.a(in_7), .b(in_23), .Cin(fulladder_8_cout), .Cout(fulladder_7_cout), .Sum(o7));
  FullAdder fulladder_8 (.a(in_8), .b(in_24), .Cin(fulladder_9_cout), .Cout(fulladder_8_cout), .Sum(o8));
  FullAdder fulladder_9 (.a(x9), .b(y9), .Cin(fulladder_10_cout), .Cout(fulladder_9_cout), .Sum(o9));
  FullAdder fulladder_10 (.a(in_10), .b(in_26), .Cin(fulladder_11_cout), .Cout(fulladder_10_cout), .Sum(o10));
  FullAdder fulladder_11 (.a(in_11), .b(in_27), .Cin(fulladder_12_cout), .Cout(fulladder_11_cout), .Sum(o11));
  FullAdder fulladder_12 (.a(in_12), .b(in_28), .Cin(fulladder_13_cout), .Cout(fulladder_12_cout), .Sum(o12));
  FullAdder fulladder_13 (.a(in_13), .b(in_29), .Cin(fulladder_14_cout), .Cout(fulladder_13_cout), .Sum(o13));
  FullAdder fulladder_14 (.a(in_14), .b(in_30), .Cin(fulladder_15_cout), .Cout(fulladder_14_cout), .Sum(o14));
  FullAdder fulladder_15 (.a(in_15), .b(in_31), .Cin(fulladder_16_cout), .Cout(fulladder_15_cout), .Sum(o15));
  FullAdder fulladder_16 (.a(x16), .b(y16), .Cin(c1), .Cout(fulladder_16_cout), .Sum(o16));
endmodule

module ALU (
  input  zx,
  input  nx,
  input  f,
  input  no,
  input  x1,
  input  in_6,
  input  in_7,
  input  in_8,
  input  in_9,
  input  in_10,
  input  in_11,
  input  in_12,
  input  x9,
  input  in_14,
  input  in_15,
  input  in_16,
  input  in_17,
  input  in_18,
  input  in_19,
  input  x16,
  input  zy,
  input  ny,
  input  y1,
  input  in_24,
  input  in_25,
  input  in_26,
  input  in_27,
  input  in_28,
  input  in_29,
  input  in_30,
  input  y9,
  input  in_32,
  input  in_33,
  input  in_34,
  input  in_35,
  input  in_36,
  input  in_37,
  input  y16,
  output o1,
  output out_40,
  output out_41,
  output out_42,
  output o5,
  output out_44,
  output out_45,
  output out_46,
  output o9,
  output out_48,
  output out_49,
  output out_50,
  output o13,
  output out_52,
  output out_53,
  output o16
);

  wire fout_1_out_34, fout_1_out_35, fout_1_out_36, fout_1_out_37, fout_1_out_38, fout_1_out_39,
       fout_1_out_40, fout_1_out_41, fout_1_out_42, fout_1_out_43, fout_1_out_44, fout_1_out_45,
       fout_1_out_46, fout_1_out_47, fout_1_out_48, fout_1_out_49, notout_1_out_18, notout_1_out_19,
       notout_1_out_20, notout_1_out_21, notout_1_out_22, notout_1_out_23, notout_1_out_24, notout_1_out_25,
       notout_1_out_26, notout_1_out_27, notout_1_out_28, notout_1_out_29, notout_1_out_30, notout_1_out_31,
       notout_1_out_32, notout_1_out_33, notout_2_out_18, notout_2_out_19, notout_2_out_20, notout_2_out_21,
       notout_2_out_22, notout_2_out_23, notout_2_out_24, notout_2_out_25, notout_2_out_26, notout_2_out_27,
       notout_2_out_28, notout_2_out_29, notout_2_out_30, notout_2_out_31, notout_2_out_32, notout_2_out_33,
       zeroout_1_out_18, zeroout_1_out_19, zeroout_1_out_20, zeroout_1_out_21, zeroout_1_out_22,
       zeroout_1_out_23, zeroout_1_out_24, zeroout_1_out_25, zeroout_1_out_26, zeroout_1_out_27,
       zeroout_1_out_28, zeroout_1_out_29, zeroout_1_out_30, zeroout_1_out_31, zeroout_1_out_32,
       zeroout_1_out_33, zeroout_2_out_18, zeroout_2_out_19, zeroout_2_out_20, zeroout_2_out_21,
       zeroout_2_out_22, zeroout_2_out_23, zeroout_2_out_24, zeroout_2_out_25, zeroout_2_out_26,
       zeroout_2_out_27, zeroout_2_out_28, zeroout_2_out_29, zeroout_2_out_30, zeroout_2_out_31,
       zeroout_2_out_32, zeroout_2_out_33;

  zeroOut zeroout_1 (
    .zx(zx), .in_2(x1), .in_3(in_6), .in_4(in_7), .in_5(in_8), .in_6(in_9), .in_7(in_10), .in_8(in_11),
    .in_9(in_12), .in_10(x9), .in_11(in_14), .in_12(in_15), .in_13(in_16), .in_14(in_17), .in_15(in_18),
    .in_16(in_19), .in_17(x16), .out_18(zeroout_1_out_18), .out_19(zeroout_1_out_19),
    .out_20(zeroout_1_out_20), .out_21(zeroout_1_out_21), .out_22(zeroout_1_out_22),
    .out_23(zeroout_1_out_23), .out_24(zeroout_1_out_24), .out_25(zeroout_1_out_25),
    .out_26(zeroout_1_out_26), .out_27(zeroout_1_out_27), .out_28(zeroout_1_out_28),
    .out_29(zeroout_1_out_29), .out_30(zeroout_1_out_30), .out_31(zeroout_1_out_31),
    .out_32(zeroout_1_out_32), .out_33(zeroout_1_out_33));
  zeroOut zeroout_2 (
    .zx(zy), .in_2(y1), .in_3(in_24), .in_4(in_25), .in_5(in_26), .in_6(in_27), .in_7(in_28), .in_8(in_29),
    .in_9(in_30), .in_10(y9), .in_11(in_32), .in_12(in_33), .in_13(in_34), .in_14(in_35), .in_15(in_36),
    .in_16(in_37), .in_17(y16), .out_18(zeroout_2_out_18), .out_19(zeroout_2_out_19),
    .out_20(zeroout_2_out_20), .out_21(zeroout_2_out_21), .out_22(zeroout_2_out_22),
    .out_23(zeroout_2_out_23), .out_24(zeroout_2_out_24), .out_25(zeroout_2_out_25),
    .out_26(zeroout_2_out_26), .out_27(zeroout_2_out_27), .out_28(zeroout_2_out_28),
    .out_29(zeroout_2_out_29), .out_30(zeroout_2_out_30), .out_31(zeroout_2_out_31),
    .out_32(zeroout_2_out_32), .out_33(zeroout_2_out_33));
  notOut notout_1 (
    .nx(nx), .x1(zeroout_1_out_18), .in_3(zeroout_1_out_19), .in_4(zeroout_1_out_20),
    .in_5(zeroout_1_out_21), .x5(zeroout_1_out_22), .in_7(zeroout_1_out_23), .in_8(zeroout_1_out_24),
    .in_9(zeroout_1_out_25), .x9(zeroout_1_out_26), .in_11(zeroout_1_out_27), .in_12(zeroout_1_out_28),
    .in_13(zeroout_1_out_29), .x13(zeroout_1_out_30), .in_15(zeroout_1_out_31), .in_16(zeroout_1_out_32),
    .in_17(zeroout_1_out_33), .out_18(notout_1_out_18), .out_19(notout_1_out_19), .out_20(notout_1_out_20),
    .out_21(notout_1_out_21), .out_22(notout_1_out_22), .out_23(notout_1_out_23), .out_24(notout_1_out_24),
    .out_25(notout_1_out_25), .out_26(notout_1_out_26), .out_27(notout_1_out_27), .out_28(notout_1_out_28),
    .out_29(notout_1_out_29), .out_30(notout_1_out_30), .out_31(notout_1_out_31), .out_32(notout_1_out_32),
    .out_33(notout_1_out_33));
  notOut notout_2 (
    .nx(ny), .x1(zeroout_2_out_18), .in_3(zeroout_2_out_19), .in_4(zeroout_2_out_20),
    .in_5(zeroout_2_out_21), .x5(zeroout_2_out_22), .in_7(zeroout_2_out_23), .in_8(zeroout_2_out_24),
    .in_9(zeroout_2_out_25), .x9(zeroout_2_out_26), .in_11(zeroout_2_out_27), .in_12(zeroout_2_out_28),
    .in_13(zeroout_2_out_29), .x13(zeroout_2_out_30), .in_15(zeroout_2_out_31), .in_16(zeroout_2_out_32),
    .in_17(zeroout_2_out_33), .out_18(notout_2_out_18), .out_19(notout_2_out_19), .out_20(notout_2_out_20),
    .out_21(notout_2_out_21), .out_22(notout_2_out_22), .out_23(notout_2_out_23), .out_24(notout_2_out_24),
    .out_25(notout_2_out_25), .out_26(notout_2_out_26), .out_27(notout_2_out_27), .out_28(notout_2_out_28),
    .out_29(notout_2_out_29), .out_30(notout_2_out_30), .out_31(notout_2_out_31), .out_32(notout_2_out_32),
    .out_33(notout_2_out_33));
  fout fout_1 (
    .x1(notout_1_out_18), .in_3(notout_1_out_19), .in_4(notout_1_out_20), .in_5(notout_1_out_21),
    .in_6(notout_1_out_22), .in_7(notout_1_out_23), .in_8(notout_1_out_24), .in_9(notout_1_out_25),
    .x9(notout_1_out_26), .in_11(notout_1_out_27), .in_12(notout_1_out_28), .in_13(notout_1_out_29),
    .in_14(notout_1_out_30), .in_15(notout_1_out_31), .in_16(notout_1_out_32), .x16(notout_1_out_33),
    .y1(notout_2_out_18), .in_19(notout_2_out_19), .in_20(notout_2_out_20), .in_21(notout_2_out_21),
    .in_22(notout_2_out_22), .in_23(notout_2_out_23), .in_24(notout_2_out_24), .in_25(notout_2_out_25),
    .y9(notout_2_out_26), .in_27(notout_2_out_27), .in_28(notout_2_out_28), .in_29(notout_2_out_29),
    .in_30(notout_2_out_30), .in_31(notout_2_out_31), .in_32(notout_2_out_32), .y16(notout_2_out_33), .f(f),
    .out_34(fout_1_out_34), .out_35(fout_1_out_35), .out_36(fout_1_out_36), .out_37(fout_1_out_37),
    .out_38(fout_1_out_38), .out_39(fout_1_out_39), .out_40(fout_1_out_40), .out_41(fout_1_out_41),
    .out_42(fout_1_out_42), .out_43(fout_1_out_43), .out_44(fout_1_out_44), .out_45(fout_1_out_45),
    .out_46(fout_1_out_46), .out_47(fout_1_out_47), .out_48(fout_1_out_48), .out_49(fout_1_out_49));
  notOut notout_3 (
    .nx(no), .x1(fout_1_out_34), .in_3(fout_1_out_35), .in_4(fout_1_out_36), .in_5(fout_1_out_37),
    .x5(fout_1_out_38), .in_7(fout_1_out_39), .in_8(fout_1_out_40), .in_9(fout_1_out_41), .x9(fout_1_out_42),
    .in_11(fout_1_out_43), .in_12(fout_1_out_44), .in_13(fout_1_out_45), .x13(fout_1_out_46),
    .in_15(fout_1_out_47), .in_16(fout_1_out_48), .in_17(fout_1_out_49), .out_18(o1), .out_19(out_40),
    .out_20(out_41), .out_21(out_42), .out_22(o5), .out_23(out_44), .out_24(out_45), .out_25(out_46),
    .out_26(o9), .out_27(out_48), .out_28(out_49), .out_29(out_50), .out_30(o13), .out_31(out_52),
    .out_32(out_53), .out_33(o16));
endmodule

// Zero Out
module zeroOut (
  input  zx,
  input  in_2,
  input  in_3,
  input  in_4,
  input  in_5,
  input  in_6,
  input  in_7,
  input  in_8,
  input  in_9,
  input  in_10,
  input  in_11,
  input  in_12,
  input  in_13,
  input  in_14,
  input  in_15,
  input  in_16,
  input  in_17,
  output out_18,
  output out_19,
  output out_20,
  output out_21,
  output out_22,
  output out_23,
  output out_24,
  output out_25,
  output out_26,
  output out_27,
  output out_28,
  output out_29,
  output out_30,
  output out_31,
  output out_32,
  output out_33
);

  wire not_1_out;

  not not_1 (not_1_out, zx);
  and and_1 (out_18, not_1_out, in_2);
  and and_2 (out_19, not_1_out, in_3);
  and and_3 (out_20, not_1_out, in_4);
  and and_4 (out_21, not_1_out, in_5);
  and and_5 (out_22, not_1_out, in_6);
  and and_6 (out_23, not_1_out, in_7);
  and and_7 (out_24, not_1_out, in_8);
  and and_8 (out_25, not_1_out, in_9);
  and and_9 (out_26, not_1_out, in_10);
  and and_10 (out_27, not_1_out, in_11);
  and and_11 (out_28, not_1_out, in_12);
  and and_12 (out_29, not_1_out, in_13);
  and and_13 (out_30, not_1_out, in_14);
  and and_14 (out_31, not_1_out, in_15);
  and and_15 (out_32, not_1_out, in_16);
  and and_16 (out_33, not_1_out, in_17);
endmodule

// not Out
module notOut (
  input  nx,
  input  x1,
  input  in_3,
  input  in_4,
  input  in_5,
  input  x5,
  input  in_7,
  input  in_8,
  input  in_9,
  input  x9,
  input  in_11,
  input  in_12,
  input  in_13,
  input  x13,
  input  in_15,
  input  in_16,
  input  in_17,
  output out_18,
  output out_19,
  output out_20,
  output out_21,
  output out_22,
  output out_23,
  output out_24,
  output out_25,
  output out_26,
  output out_27,
  output out_28,
  output out_29,
  output out_30,
  output out_31,
  output out_32,
  output out_33
);

  xor xor_1 (out_18, x1, nx);
  xor xor_2 (out_19, nx, in_3);
  xor xor_3 (out_20, in_4, nx);
  xor xor_4 (out_21, nx, in_5);
  xor xor_5 (out_22, x5, nx);
  xor xor_6 (out_23, nx, in_7);
  xor xor_7 (out_24, in_8, nx);
  xor xor_8 (out_25, nx, in_9);
  xor xor_9 (out_26, x9, nx);
  xor xor_10 (out_27, nx, in_11);
  xor xor_11 (out_28, in_12, nx);
  xor xor_12 (out_29, nx, in_13);
  xor xor_13 (out_30, x13, nx);
  xor xor_14 (out_31, nx, in_15);
  xor xor_15 (out_32, in_16, nx);
  xor xor_16 (out_33, nx, in_17);
endmodule

// function selector
module fout (
  input  f,
  input  x1,
  input  in_3,
  input  in_4,
  input  in_5,
  input  in_6,
  input  in_7,
  input  in_8,
  input  in_9,
  input  x9,
  input  in_11,
  input  in_12,
  input  in_13,
  input  in_14,
  input  in_15,
  input  in_16,
  input  x16,
  input  y1,
  input  in_19,
  input  in_20,
  input  in_21,
  input  in_22,
  input  in_23,
  input  in_24,
  input  in_25,
  input  y9,
  input  in_27,
  input  in_28,
  input  in_29,
  input  in_30,
  input  in_31,
  input  in_32,
  input  y16,
  output out_34,
  output out_35,
  output out_36,
  output out_37,
  output out_38,
  output out_39,
  output out_40,
  output out_41,
  output out_42,
  output out_43,
  output out_44,
  output out_45,
  output out_46,
  output out_47,
  output out_48,
  output out_49
);

  wire bitand_1_out_33, bitand_1_out_34, bitand_1_out_35, bitand_1_out_36, bitand_1_out_37, bitand_1_out_38,
       bitand_1_out_39, bitand_1_out_40, bitand_1_out_41, bitand_1_out_42, bitand_1_out_43, bitand_1_out_44,
       bitand_1_out_45, bitand_1_out_46, bitand_1_out_47, bitand_1_out_48, n16bitadder_1_o1,
       n16bitadder_1_o2, n16bitadder_1_o3, n16bitadder_1_o4, n16bitadder_1_o5, n16bitadder_1_o6,
       n16bitadder_1_o7, n16bitadder_1_o8, n16bitadder_1_o9, n16bitadder_1_o10, n16bitadder_1_o11,
       n16bitadder_1_o12, n16bitadder_1_o13, n16bitadder_1_o14, n16bitadder_1_o15, n16bitadder_1_o16;

  _16bitAdder u_16bitadder_1 (
    .x1(x1), .in_2(in_3), .in_3(in_4), .in_4(in_5), .in_5(in_6), .in_6(in_7), .in_7(in_8), .in_8(in_9),
    .x9(x9), .in_10(in_11), .in_11(in_12), .in_12(in_13), .in_13(in_14), .in_14(in_15), .in_15(in_16),
    .x16(x16), .y1(y1), .in_18(in_19), .in_19(in_20), .in_20(in_21), .in_21(in_22), .in_22(in_23),
    .in_23(in_24), .in_24(in_25), .y9(y9), .in_26(in_27), .in_27(in_28), .in_28(in_29), .in_29(in_30),
    .in_30(in_31), .in_31(in_32), .y16(y16), .c1(1'b0), .o1(n16bitadder_1_o1), .o2(n16bitadder_1_o2),
    .o3(n16bitadder_1_o3), .o4(n16bitadder_1_o4), .o5(n16bitadder_1_o5), .o6(n16bitadder_1_o6),
    .o7(n16bitadder_1_o7), .o8(n16bitadder_1_o8), .o9(n16bitadder_1_o9), .o10(n16bitadder_1_o10),
    .o11(n16bitadder_1_o11), .o12(n16bitadder_1_o12), .o13(n16bitadder_1_o13), .o14(n16bitadder_1_o14),
    .o15(n16bitadder_1_o15), .o16(n16bitadder_1_o16));  // open: overflow
  bitAnd bitand_1 (
    .x1(x1), .in_2(in_3), .in_3(in_4), .in_4(in_5), .in_5(in_6), .in_6(in_7), .in_7(in_8), .in_8(in_9),
    .x9(x9), .in_10(in_11), .in_11(in_12), .in_12(in_13), .in_13(in_14), .in_14(in_15), .in_15(in_16),
    .x16(x16), .y1(y1), .in_18(in_19), .in_19(in_20), .in_20(in_21), .in_21(in_22), .in_22(in_23),
    .in_23(in_24), .in_24(in_25), .y9(y9), .in_26(in_27), .in_27(in_28), .in_28(in_29), .in_29(in_30),
    .in_30(in_31), .in_31(in_32), .y16(y16), .out_33(bitand_1_out_33), .out_34(bitand_1_out_34),
    .out_35(bitand_1_out_35), .out_36(bitand_1_out_36), .out_37(bitand_1_out_37), .out_38(bitand_1_out_38),
    .out_39(bitand_1_out_39), .out_40(bitand_1_out_40), .out_41(bitand_1_out_41), .out_42(bitand_1_out_42),
    .out_43(bitand_1_out_43), .out_44(bitand_1_out_44), .out_45(bitand_1_out_45), .out_46(bitand_1_out_46),
    .out_47(bitand_1_out_47), .out_48(bitand_1_out_48));
  _16bitFMulti u_16bitfmulti_1 (
    .f(f), .add1(n16bitadder_1_o1), .in_3(n16bitadder_1_o2), .in_4(n16bitadder_1_o3),
    .in_5(n16bitadder_1_o4), .in_6(n16bitadder_1_o5), .in_7(n16bitadder_1_o6), .in_8(n16bitadder_1_o7),
    .in_9(n16bitadder_1_o8), .add9(n16bitadder_1_o9), .in_11(n16bitadder_1_o10), .in_12(n16bitadder_1_o11),
    .in_13(n16bitadder_1_o12), .in_14(n16bitadder_1_o13), .in_15(n16bitadder_1_o14),
    .in_16(n16bitadder_1_o15), .add16(n16bitadder_1_o16), ._1(bitand_1_out_33), .in_19(bitand_1_out_34),
    .in_20(bitand_1_out_35), .in_21(bitand_1_out_36), .in_22(bitand_1_out_37), .in_23(bitand_1_out_38),
    .in_24(bitand_1_out_39), .in_25(bitand_1_out_40), ._9(bitand_1_out_41), .in_27(bitand_1_out_42),
    .in_28(bitand_1_out_43), .in_29(bitand_1_out_44), .in_30(bitand_1_out_45), .in_31(bitand_1_out_46),
    .in_32(bitand_1_out_47), ._16(bitand_1_out_48), .out_34(out_34), .out_35(out_35), .out_36(out_36),
    .out_37(out_37), .out_38(out_38), .out_39(out_39), .out_40(out_40), .out_41(out_41), .out_42(out_42),
    .out_43(out_43), .out_44(out_44), .out_45(out_45), .out_46(out_46), .out_47(out_47), .out_48(out_48),
    .out_49(out_49));
endmodule

// bit And
module bitAnd (
  input  x1,
  input  in_2,
  input  in_3,
  input  in_4,
  input  in_5,
  input  in_6,
  input  in_7,
  input  in_8,
  input  x9,
  input  in_10,
  input  in_11,
  input  in_12,
  input  in_13,
  input  in_14,
  input  in_15,
  input  x16,
  input  y1,
  input  in_18,
  input  in_19,
  input  in_20,
  input  in_21,
  input  in_22,
  input  in_23,
  input  in_24,
  input  y9,
  input  in_26,
  input  in_27,
  input  in_28,
  input  in_29,
  input  in_30,
  input  in_31,
  input  y16,
  output out_33,
  output out_34,
  output out_35,
  output out_36,
  output out_37,
  output out_38,
  output out_39,
  output out_40,
  output out_41,
  output out_42,
  output out_43,
  output out_44,
  output out_45,
  output out_46,
  output out_47,
  output out_48
);

  and and_1 (out_33, x1, y1);
  and and_2 (out_34, in_18, in_2);
  and and_3 (out_35, in_3, in_19);
  and and_4 (out_36, in_20, in_4);
  and and_5 (out_37, in_5, in_21);
  and and_6 (out_38, in_22, in_6);
  and and_7 (out_39, in_7, in_23);
  and and_8 (out_40, in_24, in_8);
  and and_9 (out_41, x9, y9);
  and and_10 (out_42, in_26, in_10);
  and and_11 (out_43, in_11, in_27);
  and and_12 (out_44, in_28, in_12);
  and and_13 (out_45, in_13, in_29);
  and and_14 (out_46, in_30, in_14);
  and and_15 (out_47, in_15, in_31);
  and and_16 (out_48, y16, x16);
endmodule

module fMulti (
  input  f,
  input  add,
  input  in_3,
  output out_4
);

  wire and_1_out, and_2_out, not_1_out;

  and and_1 (and_1_out, f, add);
  not not_1 (not_1_out, f);
  and and_2 (and_2_out, not_1_out, in_3);
  or or_1 (out_4, and_1_out, and_2_out);
endmodule

// selector
module _16bitFMulti (
  input  f,
  input  add1,
  input  in_3,
  input  in_4,
  input  in_5,
  input  in_6,
  input  in_7,
  input  in_8,
  input  in_9,
  input  add9,
  input  in_11,
  input  in_12,
  input  in_13,
  input  in_14,
  input  in_15,
  input  in_16,
  input  add16,
  input  _1,
  input  in_19,
  input  in_20,
  input  in_21,
  input  in_22,
  input  in_23,
  input  in_24,
  input  in_25,
  input  _9,
  input  in_27,
  input  in_28,
  input  in_29,
  input  in_30,
  input  in_31,
  input  in_32,
  input  _16,
  output out_34,
  output out_35,
  output out_36,
  output out_37,
  output out_38,
  output out_39,
  output out_40,
  output out_41,
  output out_42,
  output out_43,
  output out_44,
  output out_45,
  output out_46,
  output out_47,
  output out_48,
  output out_49
);

  fMulti fmulti_1 (.f(f), .add(add1), .in_3(_1), .out_4(out_34));
  fMulti fmulti_2 (.f(f), .add(in_3), .in_3(in_19), .out_4(out_35));
  fMulti fmulti_3 (.f(f), .add(in_4), .in_3(in_20), .out_4(out_36));
  fMulti fmulti_4 (.f(f), .add(in_5), .in_3(in_21), .out_4(out_37));
  fMulti fmulti_5 (.f(f), .add(in_6), .in_3(in_22), .out_4(out_38));
  fMulti fmulti_6 (.f(f), .add(in_7), .in_3(in_23), .out_4(out_39));
  fMulti fmulti_7 (.f(f), .add(in_8), .in_3(in_24), .out_4(out_40));
  fMulti fmulti_8 (.f(f), .add(in_9), .in_3(in_25), .out_4(out_41));
  fMulti fmulti_9 (.f(f), .add(add9), .in_3(_9), .out_4(out_42));
  fMulti fmulti_10 (.f(f), .add(in_11), .in_3(in_27), .out_4(out_43));
  fMulti fmulti_11 (.f(f), .add(in_12), .in_3(in_28), .out_4(out_44));
  fMulti fmulti_12 (.f(f), .add(in_13), .in_3(in_29), .out_4(out_45));
  fMulti fmulti_13 (.f(f), .add(in_14), .in_3(in_30), .out_4(out_46));
  fMulti fmulti_14 (.f(f), .add(in_15), .in_3(in_31), .out_4(out_47));
  fMulti fmulti_15 (.f(f), .add(in_16), .in_3(in_32), .out_4(out_48));
  fMulti fmulti_16 (.f(f), .add(add16), .in_3(_16), .out_4(out_49));
endmodule

module CPU (
  input  [15:0] Instruction,
  input  Reset_CPU,
  input  [15:0] RAM_Dout,
  output [14:0] Instr_Address,
  output [14:0] RAM_Adr,
  output [15:0] RAM_Din,
  output Str_RAM
);

  wire and_1_out, and_2_out, and_4_out, and_5_out, and_6_out, and_7_out, and_8_out, clock_1_out, clock_2_out,
       not_1_out, or_1_out, or_2_out;
  wire [15:0] Data_q, multiplexer_1_out, multiplexer_2_out;
  wire [15:15] Address_q;

  program_counter program_counter_1 (.Set(and_2_out), .set_to(RAM_Adr), .Reset(Reset_CPU), .currVal(Instr_Address));
  or or_1 (or_1_out, Instruction[5], not_1_out);
  not not_1 (not_1_out, Instruction[15]);
  and and_1 (and_1_out, Instruction[15], Instruction[5]);
  Multiplexer #(.width(16), .enable("false")) multiplexer_1 (
    .in0(Instruction), .in1(RAM_Din), .out(multiplexer_1_out), .sel(and_1_out));
  Register #(.width(16)) Address (
    .D(multiplexer_1_out), .en(or_1_out), .Q({Address_q[15], RAM_Adr}), .clk(clock_1_out), .clr(Reset_CPU));
  Clock clock_1 (.out(clock_1_out));
  and and_2 (and_2_out, or_2_out, Instruction[15]);
  Multiplexer #(.width(16), .enable("false")) multiplexer_2 (
    .in0({Address_q[15], RAM_Adr}), .in1(RAM_Dout), .out(multiplexer_2_out), .sel(Instruction[12]));
  and and_3 (Str_RAM, Instruction[15], Instruction[3]);
  and and_4 (and_4_out, Instruction[15], Instruction[4]);
  Clock clock_2 (.out(clock_2_out));
  or or_2 (or_2_out, and_7_out, and_6_out, and_5_out);
  Register #(.width(16)) Data (.D(RAM_Din), .en(and_4_out), .Q(Data_q), .clk(clock_2_out), .clr(Reset_CPU));
  and and_5 (and_5_out, Instruction[2], RAM_Din[15]);
  ALU alu_1 (
    .x1(Data_q[15]), .in_6(Data_q[14]), .in_7(Data_q[13]), .in_8(Data_q[12]), .in_9(Data_q[11]),
    .in_10(Data_q[10]), .in_11(Data_q[9]), .in_12(Data_q[8]), .x9(Data_q[7]), .in_14(Data_q[6]),
    .in_15(Data_q[5]), .in_16(Data_q[4]), .in_17(Data_q[3]), .in_18(Data_q[2]), .in_19(Data_q[1]),
    .x16(Data_q[0]), .y1(multiplexer_2_out[15]), .in_24(multiplexer_2_out[14]),
    .in_25(multiplexer_2_out[13]), .in_26(multiplexer_2_out[12]), .in_27(multiplexer_2_out[11]),
    .in_28(multiplexer_2_out[10]), .in_29(multiplexer_2_out[9]), .in_30(multiplexer_2_out[8]),
    .y9(multiplexer_2_out[7]), .in_32(multiplexer_2_out[6]), .in_33(multiplexer_2_out[5]),
    .in_34(multiplexer_2_out[4]), .in_35(multiplexer_2_out[3]), .in_36(multiplexer_2_out[2]),
    .in_37(multiplexer_2_out[1]), .y16(multiplexer_2_out[0]), .o1(RAM_Din[15]), .out_40(RAM_Din[14]),
    .out_41(RAM_Din[13]), .out_42(RAM_Din[12]), .o5(RAM_Din[11]), .out_44(RAM_Din[10]), .out_45(RAM_Din[9]),
    .out_46(RAM_Din[8]), .o9(RAM_Din[7]), .out_48(RAM_Din[6]), .out_49(RAM_Din[5]), .out_50(RAM_Din[4]),
    .o13(RAM_Din[3]), .out_52(RAM_Din[2]), .out_53(RAM_Din[1]), .o16(RAM_Din[0]), .zx(Instruction[11]),
    .zy(Instruction[9]), .nx(Instruction[10]), .ny(Instruction[8]), .f(Instruction[7]), .no(Instruction[6]));
  and and_6 (and_6_out, Instruction[0], ~RAM_Din[15], ~and_8_out);  // AND_Gate
  and and_7 (and_7_out, Instruction[1], and_8_out);
  and and_8 (and_8_out, ~RAM_Din[8], ~RAM_Din[15], ~RAM_Din[14], ~RAM_Din[13], ~RAM_Din[12], ~RAM_Din[11], ~RAM_Din[10], ~RAM_Din[9], ~RAM_Din[7], ~RAM_Din[6], ~RAM_Din[5], ~RAM_Din[4], ~RAM_Din[3], ~RAM_Din[2], ~RAM_Din[1], ~RAM_Din[0]);  // AND_Gate
endmodule

module program_counter (
  input  Set,
  input  [14:0] set_to,
  input  Reset,
  output [14:0] currVal
);

  wire adder_1_cout, clock_1_out, not_1_out;
  wire [14:0] adder_1_out, bit_extender_1_out, multiplexer_1_out;

  not not_1 (not_1_out, Set);
  Multiplexer #(.width(15), .enable("false")) multiplexer_1 (
    .in0(set_to), .in1(adder_1_out), .out(multiplexer_1_out), .sel(not_1_out));
  Clock clock_1 (.out(clock_1_out));
  Register #(.width(15)) register_1 (.D(multiplexer_1_out), .en(1'b1), .Q(currVal), .clk(clock_1_out), .clr(Reset));
  assign bit_extender_1_out = {{14{1'b0}}, 1'b0};  // Bit_Extender bit_extender_1
  // Probe on adder_1_cout
  Adder #(.width(15)) adder_1 (.a(currVal), .b(bit_extender_1_out), .out(adder_1_out), .cin(1'b1), .cout(adder_1_cout));
endmodule

module computer (
  input  Reset
);

  wire clock_1_out, cpu_1_p7;
  wire [14:0] cpu_1_p3, cpu_1_p4;
  wire [15:0] cpu_1_p2, cpu_1_p6, rom_1_data;

  ROM #(.addrWidth(15), .dataWidth(16)) rom_1 (.addr(cpu_1_p3), .data(rom_1_data), .sel(1'b1));
  // CPU cpu_1: pin names not known; wires that end beside it: Reset, cpu_1_p2, cpu_1_p3, cpu_1_p4, rom_1_data, cpu_1_p6, cpu_1_p7
  RAM #(.addrWidth(15), .dataWidth(16), .bus("separate")) ram_1 (
    .addr(cpu_1_p4), .din(cpu_1_p2), .data(cpu_1_p6), .str(cpu_1_p7), .sel(1'b1), .clk(clock_1_out),
    .ld(1'b1), .clr(Reset));
  Clock clock_1 (.out(clock_1_out));

  // Notes on the sheet:
  //   contents of rom_1 (hex, n*v repeats v):
  //   7 ec10 0 e308 4 ec10 1 e308 2 ea88 10 efc8 0 fc10 2 f088 10 fdc8 fc10 1 f4d0 c e306 17 ea87
endmodule
